# Fritzing sketch UC_Halfwaythrough_SmartPillow (saved by Fritzing 0.6.3b)
breadboards: 1

parts:
  R1 = Resistor [tolerance=±5% resistance=220 package=THT]
  R2 = Resistor [tolerance=±5% resistance=220 package=THT]
  Arduino1 = Arduino
  J1 = Basic Force Sensing Resistor (FSR) [package=THT]
  J2 = Basic Force Sensing Resistor (FSR) [package=THT]
  Part1 = Bluetooth Mate Silver

nets:
  GND: R1.Pin_0, R2.Pin_0, Arduino1.GND, Part1.GND
  N1: R1.Pin_1, Arduino1.A0, J1.pin_1
  N2: R2.Pin_1, Arduino1.A1, J2.pin_0
  N3: Arduino1.D1TX, Part1.RX_5V
  N4: Arduino1.D0RX, Part1.TX_5V
  +5V: Arduino1.+5V, J1.pin_0, J2.pin_1, Part1.VCC
  N5: Part1.RTS_5V, Part1.CTS_5V
